# Fritzing sketch CeCe_1_SterlingPowers_Midterm (saved by Fritzing 1.0.4)
breadboards: 1

parts:
  SP1 = SPEAKER [package=pcb_mount_speaker]
  OLED_I2C1 = OLED 128x64 I2C Monochrome Display
  R1 = Resistor [tolerance=±5% power=0.25W resistance=220 package=THT]
  SW1 = ENCODER_RGB_CA [package=encoder_led_3]
  DFRobot_DFPlayer_Mini1 = DFRobot DFPlayer Mini [part_number=DFR0299]
  S1 = Pushbutton [package="[THT]"]
  A1 = Particle - Photon2

nets (from the schematic view):
  N1: SP1.+, DFRobot_DFPlayer_Mini1.SPK_2
  N2: SP1.-, DFRobot_DFPlayer_Mini1.SPK_1
  N3: OLED_I2C1.SDA, A1.Pin_17
  N4: OLED_I2C1.SCK, A1.Pin_18
  VDD: OLED_I2C1.VDD, R1.Pin_0, DFRobot_DFPlayer_Mini1.VCC, S1.Pin_3, S1.Pin_4, A1.Pin_2, A1.Pin_31
  N5: OLED_I2C1.GND, R1.Pin_1, SW1.C, DFRobot_DFPlayer_Mini1.GND-1, DFRobot_DFPlayer_Mini1.GND-2, A1.Pin_4, A1.Pin_32
  N6: SW1.SW, A1.Pin_20
  N7: SW1.A, A1.Pin_21
  N8: SW1.B, A1.Pin_22
  N9: DFRobot_DFPlayer_Mini1.RX, A1.Pin_14
  N10: DFRobot_DFPlayer_Mini1.TX, A1.Pin_15
  N11: S1.Pin_1, S1.Pin_2, A1.Pin_19

custom parts:
  Pushbutton: A generic pushbutton.
  Particle - Photon2: The Photon 2 is a microcontroller and Wi-Fi networking developed by particle. Features: 802.11a/b/g/n Wi-Fi, 2.4 GHz and 5 GHz Integrated PCB antenna Integrated U.FL connector for external antenna Integrated RF switch BLE 5 using same antenna as Wi-Fi Realtek RTL8721DM MCU ARM Cortex M33 CPU, 200 MHz 2048 KB (2 MB) user application maximum size 3072 KB (3 MB) of RAM available to user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
